# Fritzing sketch şematik (saved by Fritzing 0.9.3b)
breadboards: 1

parts:
  Parça1 = Arduino Mega 2560 (Rev3)
  J1 = Basic Servo
  J2 = Basic Servo
  J3 = Basic Servo
  J4 = Basic Servo
  U3 = LIPO-2000mAh [package=lipo-2000]
  Parça2 = Power Cell LiPo Charger/Booster
  Parça3 = Thumb Joystick
  Parça4 = Thumb Joystick

nets:
  N1: Parça1.A1, Parça4.VERT
  N2: Parça1.A2, Parça4.HORZ
  N3: Parça1.A3, Parça3.VERT
  N4: Parça1.A4, Parça3.HORZ
  GND: Parça1.GND, J1.gnd, J2.gnd, J3.gnd, J4.gnd, U3.-, Parça2.GND, Parça3.GND, Parça4.GND
  VCC: Parça1.VIN, J1.vcc, J2.vcc, J3.vcc, J4.vcc, Parça2.5VIN, Parça3.VCC, Parça4.VCC
  N5: Parça1.D4_PWM, J1.pulse
  N6: Parça1.D5_PWM, J4.pulse
  N7: Parça1.D6_PWM, J2.pulse
  N8: Parça1.D7_PWM, J3.pulse
  N9: U3.+, Parça2.VCC
